// Logisim project Ash Exp11.circ as structural Verilog: 1 circuit, main circuit main
module main (
  input  A,
  input  B,
  output SUM,
  output CARRY
);

  wire _1_out, _2_out, _3_out;

  nand _1 (_1_out, A, B);
  nand _2 (_2_out, A, _1_out);
  nand _3 (_3_out, _1_out, B);
  nand _4 (SUM, _2_out, _3_out);
  nand _5 (CARRY, _1_out, _1_out);

  // Notes on the sheet:
  //   2-BIT HALF ADDER USING NAND GATE
endmodule
