// Logisim project Ash Exp8.circ as structural Verilog: 1 circuit, main circuit main
module main (
  input  in_1,
  input  in_2,
  output SUM,
  output CARRY
);

  xor XOR (SUM, in_1, in_2);
  and AND (CARRY, in_1, in_2);

  // Notes on the sheet:
  //   2-BIT HALF ADDER
endmodule
